// Logisim project SOMADOR 4 BIT.circ as structural Verilog: 2 circuits, main circuit ADD-1
module ADD_1 (
  input  A,
  input  B,
  input  C,
  output S,
  output V
);

  wire and_1_out, and_2_out, and_3_out, and_4_out, and_5_out, and_6_out, and_7_out, and_8_out;

  and and_1 (and_1_out, ~A, ~B, C);  // AND_Gate
  and and_2 (and_2_out, ~A, B, ~C);  // AND_Gate
  and and_3 (and_3_out, A, ~B, ~C);  // AND_Gate
  and and_4 (and_4_out, A, B, C);
  and and_5 (and_5_out, ~A, B, C);  // AND_Gate
  and and_6 (and_6_out, A, ~B, C);  // AND_Gate
  and and_7 (and_7_out, A, B, ~C);  // AND_Gate
  and and_8 (and_8_out, A, B, C);
  or or_1 (S, and_1_out, and_2_out, and_3_out, and_4_out);
  or or_2 (V, and_5_out, and_6_out, and_7_out, and_8_out);
endmodule

module ADD_4 (
  input  [3:0] A,
  input  [3:0] B,
  input  in_3,
  output overflow,
  output [3:0] out_5
);

  wire add_1_2_v, add_1_3_v, add_1_4_v;

  // Probe on B
  ADD_1 add_1_1 (.S(out_5[3]), .V(overflow), .A(B[3]), .B(A[3]), .C(add_1_3_v));
  // Probe on A
  ADD_1 add_1_2 (.S(out_5[1]), .V(add_1_2_v), .A(B[1]), .B(A[1]), .C(add_1_4_v));
  ADD_1 add_1_3 (.S(out_5[2]), .V(add_1_3_v), .A(B[2]), .B(A[2]), .C(add_1_2_v));
  // Probe on out_5
  ADD_1 add_1_4 (.S(out_5[0]), .V(add_1_4_v), .A(B[0]), .B(A[0]), .C(in_3));
endmodule
